// Logisim project hw4.circ as structural Verilog: 5 circuits, main circuit one hot state machine
module one_hot_state_machine (
  input  CLK,
  input  H,
  input  RST,
  output A,
  output B,
  output C,
  output D
);

  wire _0, _1, _2, _3, _4, _4____5, _5, _5____5, and_4_out, or_6_out, Out5, Start, State_0_3, State_0_5,
       State_1, State_2, State_3, State_3_4, State_4, State_4_0, State_5, State_5_4;
  wire [5:0] or_2_out;

  or or_1 (or_2_out[4], State_4_0, State_4);
  or or_2 (or_2_out[0], Start, State_0_5, State_0_3);
  or or_3 (or_2_out[3], State_3, State_3_4);
  or or_4 (Out5, _4____5, _5____5);
  or or_5 (or_2_out[5], State_5, State_5_4);
  not not_1 (Start, or_6_out);
  Register #(.width(6)) register_1 (
    .D({or_2_out[5:3], State_2, State_1, or_2_out[0]}), .Q({_5, _4, _3, _2, _1, _0}), .clk(CLK), .clr(RST));  // open: en
  or or_6 (or_6_out, _0, _1, _2, _3, _4, _5);
  and and_1 (State_4_0, ~H, _0);  // AND_Gate
  and and_2 (State_1, _0, H);
  and and_3 (State_5_4, H, _4);
  or or_7 (A, _0, _4);
  or or_8 (B, _1, _3);
  or or_9 (C, _4, _5);
  or or_10 (D, _2, _3);
  and and_4 (and_4_out, ~H, _2);  // AND_Gate
  or or_11 (State_2, _1, and_4_out);
  and and_5 (State_3_4, _4, ~H);  // AND_Gate
  and and_6 (State_0_3, ~H, _3);  // AND_Gate
  and and_7 (State_3, _2, H);
  and and_8 (State_5, H, _5);
  and and_9 (State_4, _3, H);
  and and_10 (State_0_5, _5, ~H);  // AND_Gate

  // Notes on the sheet:
  //   Do not place anything here!
  //   Moving the input and output pins of this subcircuit will break the tester subcircuit
endmodule

module one_hot_tester (
  input  H
);

  wire CLK_out, one_hot_state_machine_1_a, one_hot_state_machine_1_b, one_hot_state_machine_1_c,
       one_hot_state_machine_1_d, RST_out;

  Clock CLK (.out(CLK_out));
  Button RST (.out(RST_out));
  one_hot_state_machine one_hot_state_machine_1 (
    .CLK(CLK_out), .H(H), .RST(RST_out), .A(one_hot_state_machine_1_a), .B(one_hot_state_machine_1_b),
    .C(one_hot_state_machine_1_c), .D(one_hot_state_machine_1_d));
  LED led_1 (.in(one_hot_state_machine_1_a));
  LED led_2 (.in(one_hot_state_machine_1_b));
  LED led_3 (.in(one_hot_state_machine_1_c));
  LED led_4 (.in(one_hot_state_machine_1_d));
endmodule

module reduced_state_machine (
  input  CLK,
  input  H,
  input  RST,
  output A,
  output B,
  output C,
  output D
);

  wire _4____5, _5____5, and_1_out, and_2_out, and_3_out, and_4_out, and_5_out, and_6_out, and_7_out,
       and_8_out, and_9_out, L0, L1, L2, Out5, S0, S1, S2;

  and and_1 (and_1_out, H, L2);
  and and_2 (and_2_out, ~L0, H);  // AND_Gate
  and and_3 (and_3_out, ~L0, L2);  // AND_Gate
  or or_1 (S0, and_1_out, and_3_out, and_2_out);
  or or_2 (Out5, _4____5, _5____5);
  and and_4 (and_4_out, L1, ~L0);  // AND_Gate
  or or_3 (S1, and_4_out, and_5_out, and_6_out);
  Register #(.width(3)) register_1 (.D({S2, S1, S0}), .Q({L2, L1, L0}), .clk(CLK), .clr(RST));  // open: en
  and and_5 (and_5_out, L0, ~L2, ~L1);  // AND_Gate
  and and_6 (and_6_out, L2, ~H, ~L0);  // AND_Gate
  and and_7 (and_7_out, H, L2);
  and and_8 (and_8_out, L1, L0, H);
  or or_4 (S2, and_7_out, and_8_out, and_9_out);
  and and_9 (and_9_out, ~L1, ~L0, ~H, ~L2);  // AND_Gate
  and and_10 (A, ~L0, ~L1);  // AND_Gate
  and and_11 (B, L0, ~L2);  // AND_Gate
  and and_12 (C, ~L1, L2);  // AND_Gate
  and and_13 (D, ~L2, L1);  // AND_Gate

  // Notes on the sheet:
  //   Do not place anything here!
  //   Moving the input and output pins of this subcircuit will break the tester subcircuit
endmodule

module reduced_tester (
  input  H
);

  wire CLK_out, reduced_state_machine_1_a, reduced_state_machine_1_b, reduced_state_machine_1_c,
       reduced_state_machine_1_d, RST_out;

  Clock CLK (.out(CLK_out));
  Button RST (.out(RST_out));
  reduced_state_machine reduced_state_machine_1 (
    .CLK(CLK_out), .H(H), .RST(RST_out), .A(reduced_state_machine_1_a), .B(reduced_state_machine_1_b),
    .C(reduced_state_machine_1_c), .D(reduced_state_machine_1_d));
  LED led_1 (.in(reduced_state_machine_1_a));
  LED led_2 (.in(reduced_state_machine_1_b));
  LED led_3 (.in(reduced_state_machine_1_c));
  LED led_4 (.in(reduced_state_machine_1_d));
endmodule

// 0xff
module automatic_tester (
  input  in_1
);

  wire and_2_out, and_3_out, and_5_out, and_7_out, bitselector_2_out, CCLK, CLK, comparator_1_gt,
       comparator_1_lt, comparator_2_gt, comparator_2_lt, comparator_3_gt, comparator_3_lt, comparator_4_gt,
       comparator_4_lt, comparator_5_gt, comparator_6_eq, d_ff_1_q, d_ff_1_qn, d_ff_2_q, DONE, G, IRST, NCLK,
       or_1_out, or_2_out, or_3_out, or_4_out, or_5_out, or_7_out, or_8_out, TEST;
  wire [3:0] ANS, OUT1, OUT2, OUT3;
  wire [7:0] and_4_out, counter_1_q, counter_2_q, INSTR, shifter_1_out;

  Button button_1 (.out(TEST));
  Clock clock_1 (.out(CLK));
  one_hot_state_machine one_hot_state_machine_1 (
    .CLK(NCLK), .H(G), .RST(IRST), .A(OUT1[3]), .B(OUT1[2]), .C(OUT1[1]), .D(OUT1[0]));
  Counter counter_1 (.Q(counter_1_q), .clk(NCLK), .clr(in_1));  // open: load, D, count, carry
  Counter counter_2 (.Q(counter_2_q), .clk(NCLK), .clr(in_1));  // open: load, D, count, carry
  or or_1 (or_1_out, comparator_1_gt, comparator_1_lt);
  Comparator #(.width(4), .mode("unsigned")) comparator_1 (
    .a(ANS), .b(4'b0000), .gt(comparator_1_gt), .lt(comparator_1_lt));  // open: eq
  Comparator #(.width(4), .mode("unsigned")) comparator_2 (
    .a(OUT1), .b(ANS), .gt(comparator_2_gt), .lt(comparator_2_lt));  // open: eq
  or or_2 (or_2_out, comparator_2_gt, comparator_2_lt);
  Comparator #(.width(4), .mode("unsigned")) comparator_3 (
    .a(OUT2), .b(ANS), .gt(comparator_3_gt), .lt(comparator_3_lt));  // open: eq
  or or_3 (or_3_out, comparator_3_gt, comparator_3_lt);
  Comparator #(.width(4), .mode("unsigned")) comparator_4 (
    .a(OUT3), .b(ANS), .gt(comparator_4_gt), .lt(comparator_4_lt));  // open: eq
  or or_4 (or_4_out, comparator_4_gt, comparator_4_lt);
  LED ERROR_S (.in(d_ff_1_q));
  LED u_DONE (.in(and_7_out));
  and and_1 (CCLK, CLK, comparator_5_gt);
  Comparator #(.mode("unsigned")) comparator_5 (.a(counter_1_q), .b(8'h1), .gt(comparator_5_gt));  // open: eq, lt
  and and_2 (and_2_out, or_3_out, or_4_out);
  reduced_state_machine reduced_state_machine_1 (
    .CLK(CCLK), .H(G), .RST(IRST), .A(OUT2[3]), .B(OUT2[2]), .C(OUT2[1]), .D(OUT2[0]));
  ROM rom_1 (.addr(counter_2_q), .data(INSTR), .sel(1'b1));
  and and_3 (and_3_out, or_1_out, or_5_out);
  or or_5 (or_5_out, or_2_out, and_2_out);
  BitSelector bitselector_1 (.in(INSTR), .out(G), .sel(3'b000));
  BitSelector bitselector_2 (.in(INSTR), .out(bitselector_2_out), .sel(3'b001));
  BitSelector bitselector_3 (.in(INSTR), .out(DONE), .sel(3'b010));
  assign and_4_out = 8'hf0 & INSTR;  // AND_Gate and_4, 8 bits wide
  Comparator #(.mode("unsigned")) comparator_6 (.a(INSTR), .b({8{1'b0}}), .eq(comparator_6_eq));  // open: gt, lt
  or or_6 (IRST, bitselector_2_out, in_1);
  Shifter #(.shift("lr")) shifter_1 (.in(and_4_out), .\dist (3'b100), .out(shifter_1_out));
  Bit_Extender #(.out_width(4)) bit_extender_1 (.in(shifter_1_out), .out(ANS));
  and and_5 (and_5_out, ~d_ff_1_q, NCLK);  // AND_Gate
  D_Flip_Flop d_ff_1 (
    .clk(and_5_out), .D(and_3_out), .Q(d_ff_1_q), .Qn(d_ff_1_qn), .preset(1'b0), .en(1'b1), .reset(in_1));
  or or_7 (or_7_out, CCLK, comparator_6_eq);
  or or_8 (or_8_out, CLK, DONE);
  D_Flip_Flop d_ff_2 (.clk(TEST), .D(1'b1), .Q(d_ff_2_q), .preset(1'b0), .en(1'b1), .reset(in_1));  // open: Qn
  reduced_state_machine reduced_state_machine_2 (
    .CLK(or_7_out), .H(G), .RST(IRST), .A(OUT3[3]), .B(OUT3[2]), .C(OUT3[1]), .D(OUT3[0]));
  and and_6 (NCLK, or_8_out, d_ff_2_q);
  and and_7 (and_7_out, d_ff_1_qn, DONE);

  // Other names for the same wires on the sheet: RST = in_1

  // Notes on the sheet:
  //   Press Ctrl+k to enable ticks, then click TEST to run the tester. You can press Ctrl+r to reset it.
  //   contents of rom_1 (hex, n*v repeats v):
  //   0 81 41 10 11 50 81 40 11 51 a0 50 80 a1 21 20 80 2 0 81 4f
  //   If there are errors with your circuit, "ERROR(S)" will be red, or there will be blue or red wires present when the tester is DONE running.
endmodule
